# Fritzing sketch Random numebr generator (saved by Fritzing 0.9.3b)
breadboards: 1
perfboards: 1

parts:
  S1 = Pushbutton [package="[THT]"]
  Деталь1 = Arduino Uno (Rev3)
  R2 = Resistor [tolerance=±5% resistance=1M package=THT]
  R5 = Resistor [tolerance=±5% resistance=1M package=THT]
  R6 = Resistor [tolerance=±5% resistance=1M package=THT]
  R7 = Resistor [tolerance=±5% resistance=1M package=THT]
  R8 = Resistor [tolerance=±5% resistance=1M package=THT]
  7_Segment1 = 7 Segment Display
  R9 = Resistor [tolerance=±5% resistance=220 package=THT]
  R10 = Resistor [tolerance=±5% resistance=220 package=THT]
  R11 = Resistor [tolerance=±5% resistance=220 package=THT]
  R12 = Resistor [tolerance=±5% resistance=220 package=THT]
  R13 = Resistor [tolerance=±5% resistance=220 package=THT]
  R14 = Resistor [tolerance=±5% resistance=220 package=THT]
  R15 = Resistor [tolerance=±5% resistance=220 package=THT]
  R16 = Resistor [tolerance=±5% resistance=220 package=THT]

nets:
  N1: S1.Pin_1, S1.Pin_2, Деталь1.D11_PWM/MOSI
  N2: S1.Pin_3, S1.Pin_4, Деталь1.5V, R2.Pin_0
  N3: Деталь1.A0, R5.Pin_0, R6.Pin_1
  N4: Деталь1.D8, R13.Pin_0
  N5: Деталь1.D9_PWM, R12.Pin_1
  N6: Деталь1.D2, R9.Pin_1
  N7: Деталь1.D3_PWM, R10.Pin_1
  N8: Деталь1.D4, R11.Pin_1
  N9: Деталь1.D5_PWM, R16.Pin_0
  N10: Деталь1.D6_PWM, R15.Pin_0
  N11: Деталь1.D7, R14.Pin_0
  N12: Деталь1.GND, R5.Pin_1, 7_Segment1.common_anode
  N13: R2.Pin_1, R8.Pin_0
  N14: R6.Pin_0, R7.Pin_1
  N15: R7.Pin_0, R8.Pin_1
  N16: 7_Segment1.Segment_G, R13.Pin_1
  N17: 7_Segment1.Segment_F, R14.Pin_1
  N18: 7_Segment1.Segment_E, R15.Pin_1
  N19: 7_Segment1.Segment_D, R16.Pin_1
  N20: 7_Segment1.Segment_DP, R12.Pin_0
  N21: 7_Segment1.Segment_C, R11.Pin_0
  N22: 7_Segment1.Segment_B, R10.Pin_0
  N23: 7_Segment1.Segment_A, R9.Pin_0

// code stored in the sketch: Random number generator.ino
int num_array[10][7] = {  { 1,1,1,1,1,1,0 },    // 0
                          { 0,1,1,0,0,0,0 },    // 1
                          { 1,1,0,1,1,0,1 },    // 2
                          { 1,1,1,1,0,0,1 },    // 3
                          { 0,1,1,0,0,1,1 },    // 4
                          { 1,0,1,1,0,1,1 },    // 5
                          { 1,0,1,1,1,1,1 },    // 6
                          { 1,1,1,0,0,0,0 },    // 7
                          { 1,1,1,1,1,1,1 },    // 8
                          { 1,1,1,0,0,1,1 }};   // 9
                                       
//void Num_Write(int);

int val = 0;

const int buttonPin = 11;    
const int ledPin =  LED_BUILTIN; 

int buttonState = 0; 

void setup() 
{ 
  pinMode(2, OUTPUT);   
  pinMode(3, OUTPUT);
  pinMode(4, OUTPUT);
  pinMode(5, OUTPUT);
  pinMode(6, OUTPUT);
  pinMode(7, OUTPUT);
  pinMode(8, OUTPUT);
  pinMode(9, OUTPUT);
  pinMode(A0, INPUT); 
  pinMode(ledPin, OUTPUT);
  pinMode(buttonPin, INPUT);

  analogReference(INTERNAL); //Set to 0 - 1.1V range
  
  Serial.begin(9600);   
}

void loop() 
{
  buttonState = digitalRead(buttonPin);
   val = analogRead(A0);
   Serial.println(val);
   
  if (buttonState == LOW) {
    delay(100);
    Num_Write(val % 10);
    digitalWrite(ledPin, LOW);
    digitalWrite(9, LOW);
  } else {
    digitalWrite(ledPin, HIGH);
    digitalWrite(9, HIGH);
  }
}

// this functions writes values to the sev seg pins  
void Num_Write(int number) 
{
  int pin= 2;
  for (int j=0; j < 7; j++) {
   digitalWrite(pin, num_array[number][j]);
   pin++;
  }
}
